# Fritzing sketch Schema (saved by Fritzing 0.9.3b)
breadboards: 1

parts:
  PIR2 = PIR sensor
  Componente2 = Arduino Uno (Rev3) - ICSP
  LED4 = smd LED [color="Green (555nm)" package="0603 [SMD]"]  # not connected
  LED5 = smd LED [color="Green (555nm)" package="0603 [SMD]"]
  R6 = Resistor [tolerance=±5% resistance=220 package=THT]
  R7 = Resistor [tolerance=±5% resistance=220 package=THT]
  R8 = Resistor [tolerance=±5% resistance=220 package=THT]
  LED6 = smd LED [color="Red (633nm)" package="0603 [SMD]"]
  S3 = Pushbutton [package="[SMD]"]
  S4 = Pushbutton [package="[SMD]"]
  R9 = Resistor [tolerance=±5% resistance=10k package="0402 [SMD]"]
  R10 = Resistor [tolerance=±5% resistance=10k package="0402 [SMD]"]
  hc-sr2 = hc-sr04

nets:
  VDD: PIR2.VDD, Componente2.5V, S3.Pin_1, S3.Pin_2, S4.Pin_1, S4.Pin_2, hc-sr2.VCC
  N1: PIR2.SIG, Componente2.D9_PWM
  GND: PIR2.GND, Componente2.GND, LED5.cathode, LED6.cathode, R9.Pin_0, R10.Pin_0, hc-sr2.GND
  N2: Componente2.D8, hc-sr2.Trig
  N3: Componente2.D10_PWM/SS, S3.Pin_3, S3.Pin_4, R10.Pin_1
  N4: Componente2.D11_PWM/MOSI, S4.Pin_3, S4.Pin_4, R9.Pin_1
  N5: Componente2.D4, R7.Pin_0
  N6: Componente2.D5_PWM, R6.Pin_0
  N7: Componente2.D6_PWM, R8.Pin_0
  N8: Componente2.D7, hc-sr2.Echo
  N9: LED5.anode, R6.Pin_1
  N10: R8.Pin_1, LED6.anode

// code stored in the sketch: pir_sensor.ino
/* The sensor's output pin goes to HIGH if motion is present.
 * However, even if motion is present, it goes to LOW from time to time, 
 * which might give the impression no motion is present. 
 * This program deals with this issue by ignoring LOW-phases shorter than a given time, 
 * assuming continuous motion is present during these phases.
 *  
 */

/////////////////////////////
//VARS
int calibrationTime = 30; //the time we give the sensor to calibrate (10-60 secs according to the datasheet)       
long unsigned int lowIn;  //the time when the sensor outputs a low impulse
long unsigned int pause = 5000;  //the amount of milliseconds the sensor has to be low before we assume all motion has stopped

boolean lockLow = true;
boolean takeLowTime;  

int pirPin = 2;    //the digital pin connected to the PIR sensor's output
//int ledPin = 13;


/////////////////////////////
//SETUP
void setup(){
  Serial.begin(9600);
  pinMode(pirPin, INPUT);
  //pinMode(ledPin, OUTPUT);
  digitalWrite(pirPin, LOW); //No movement at the beginning

  //give the sensor some time to calibrate
  Serial.print("calibrating sensor ");
    for(int i = 0; i < calibrationTime; i++){
      Serial.print(".");
      delay(1000);
      }
    Serial.println(" done");
    Serial.println("SENSOR ACTIVE");
    delay(50);
  }

////////////////////////////
//LOOP
void loop(){

  if(digitalRead(pirPin) == HIGH){
      //digitalWrite(ledPin, HIGH);   //the led visualizes the sensors output pin state
      if(lockLow){  
         //makes sure we wait for a transition to LOW before any further output is made:
         lockLow = false;            
         Serial.println("---");
         Serial.print("motion detected at ");
         Serial.print(millis()/1000);
         Serial.println(" sec"); 
         delay(50);
         }         
       takeLowTime = true;
  }

  if(digitalRead(pirPin) == LOW){       
       //digitalWrite(ledPin, LOW);  //the led visualizes the sensors output pin state
       if(takeLowTime){
          lowIn = millis();          //save the time of the transition from high to LOW
          takeLowTime = false;       //make sure this is only done at the start of a LOW phase
       }
       //if the sensor is low for more than the given pause, 
       //we assume that no more motion is going to happen
       if(!lockLow && millis() - lowIn > pause){  
           //makes sure this block of code is only executed again after 
           //a new motion sequence has been detected
           lockLow = true;                        
           Serial.print("motion ended at ");      //output
           Serial.print((millis() - pause)/1000);
           Serial.println(" sec");
           delay(50);
       }
  }
}
